// Logisim project CSE332_Rahiq_Tazrian.circ as structural Verilog
module _1_bit_ALU (
  input  A,
  input  B,
  input  CarryIn,
  input  [1:0] S1S0,
  output Result,
  output Cout
);

  wire adder_1_out, and_1_out, and_2_out, multiplexer_1_out, not_1_out, or_1_out;

  Multiplexer #(.enable("false")) multiplexer_1 (.in0(B), .in1(not_1_out), .out(multiplexer_1_out), .sel(and_1_out));
  not not_1 (not_1_out, B);
  and and_1 (and_1_out, S1S0[0], S1S0[1]);
  and and_2 (and_2_out, A, B);
  or or_1 (or_1_out, A, B);
  Adder #(.width(1)) adder_1 (.a(A), .b(multiplexer_1_out), .out(adder_1_out), .cin(CarryIn), .cout(Cout));
  Multiplexer #(.select(2), .enable("false")) multiplexer_2 (
    .in0(and_2_out), .in1(or_1_out), .in2(adder_1_out), .in3(adder_1_out), .out(Result), .sel(S1S0));
endmodule

module _32_bit_ALU (
  input  CarryIn,
  input  [15:0] A,
  input  [15:0] B,
  input  [1:0] S1S0,
  output [15:0] Result,
  output Cout
);

  wire main_1_cout, main_2_cout, main_3_cout, main_4_cout, main_5_cout, main_6_cout, main_7_cout,
       main_8_cout, main_9_cout, main_10_cout, main_11_cout, main_12_cout, main_13_cout, main_14_cout,
       main_15_cout;

  Lab_6_16_bit_alu_main main_1 (
    .A(A[0]), .B(B[0]), .CarryIn(CarryIn), .S1S0(S1S0), .Result(Result[0]), .Cout(main_1_cout));
  Lab_6_16_bit_alu_main main_2 (
    .A(A[1]), .B(B[1]), .CarryIn(main_1_cout), .S1S0(S1S0), .Result(Result[1]), .Cout(main_2_cout));
  Lab_6_16_bit_alu_main main_3 (
    .A(A[2]), .B(B[2]), .CarryIn(main_2_cout), .S1S0(S1S0), .Result(Result[2]), .Cout(main_3_cout));
  Lab_6_16_bit_alu_main main_4 (
    .A(A[3]), .B(B[3]), .CarryIn(main_3_cout), .S1S0(S1S0), .Result(Result[3]), .Cout(main_4_cout));
  Lab_6_16_bit_alu_main main_5 (
    .A(A[4]), .B(B[4]), .CarryIn(main_4_cout), .S1S0(S1S0), .Result(Result[4]), .Cout(main_5_cout));
  Lab_6_16_bit_alu_main main_6 (
    .A(A[5]), .B(B[5]), .CarryIn(main_5_cout), .S1S0(S1S0), .Result(Result[5]), .Cout(main_6_cout));
  Lab_6_16_bit_alu_main main_7 (
    .A(A[6]), .B(B[6]), .CarryIn(main_6_cout), .S1S0(S1S0), .Result(Result[6]), .Cout(main_7_cout));
  Lab_6_16_bit_alu_main main_8 (
    .A(A[7]), .B(B[7]), .CarryIn(main_7_cout), .S1S0(S1S0), .Result(Result[7]), .Cout(main_8_cout));
  Lab_6_16_bit_alu_main main_9 (
    .A(A[8]), .B(B[8]), .CarryIn(main_8_cout), .S1S0(S1S0), .Result(Result[8]), .Cout(main_9_cout));
  Lab_6_16_bit_alu_main main_10 (
    .A(A[9]), .B(B[9]), .CarryIn(main_9_cout), .S1S0(S1S0), .Result(Result[9]), .Cout(main_10_cout));
  Lab_6_16_bit_alu_main main_11 (
    .A(A[10]), .B(B[10]), .CarryIn(main_10_cout), .S1S0(S1S0), .Result(Result[10]), .Cout(main_11_cout));
  Lab_6_16_bit_alu_main main_12 (
    .A(A[11]), .B(B[11]), .CarryIn(main_11_cout), .S1S0(S1S0), .Result(Result[11]), .Cout(main_12_cout));
  Lab_6_16_bit_alu_main main_13 (
    .A(A[12]), .B(B[12]), .CarryIn(main_12_cout), .S1S0(S1S0), .Result(Result[12]), .Cout(main_13_cout));
  Lab_6_16_bit_alu_main main_14 (
    .A(A[13]), .B(B[13]), .CarryIn(main_13_cout), .S1S0(S1S0), .Result(Result[13]), .Cout(main_14_cout));
  Lab_6_16_bit_alu_main main_15 (
    .A(A[14]), .B(B[14]), .CarryIn(main_14_cout), .S1S0(S1S0), .Result(Result[14]), .Cout(main_15_cout));
  Lab_6_16_bit_alu_main main_16 (
    .A(A[15]), .B(B[15]), .CarryIn(main_15_cout), .S1S0(S1S0), .Result(Result[15]), .Cout(Cout));
endmodule

module _32_bit_RF (
  input  [31:0] Data_In,
  input  Reg_Write,
  input  [4:0] Read_Address_1,
  input  [4:0] Write_Address,
  input  [4:0] Read_Address_2,
  input  in_6,
  output [31:0] Data_Out_1,
  output [31:0] Data_Out_2
);

  wire and_1_out, and_2_out, and_3_out, and_4_out, and_5_out, and_6_out, and_7_out, and_8_out, and_9_out,
       and_10_out, and_11_out, and_12_out, and_13_out, and_14_out, and_15_out, and_16_out, and_17_out,
       and_18_out, and_19_out, and_20_out, and_21_out, and_22_out, and_23_out, and_24_out, and_25_out,
       and_26_out, and_27_out, and_28_out, and_29_out, and_30_out, and_31_out, and_32_out, decoder_1_out0,
       decoder_1_out1, decoder_1_out2, decoder_1_out3, decoder_1_out4, decoder_1_out5, decoder_1_out6,
       decoder_1_out7, decoder_1_out8, decoder_1_out9, decoder_1_out10, decoder_1_out11, decoder_1_out12,
       decoder_1_out13, decoder_1_out14, decoder_1_out15, decoder_1_out16, decoder_1_out17, decoder_1_out18,
       decoder_1_out19, decoder_1_out20, decoder_1_out21, decoder_1_out22, decoder_1_out23, decoder_1_out24,
       decoder_1_out25, decoder_1_out26, decoder_1_out27, decoder_1_out28, decoder_1_out29, decoder_1_out30,
       decoder_1_out31;
  wire [31:0] register_1_q, register_2_q, register_3_q, register_4_q, register_5_q, register_6_q,
       register_7_q, register_8_q, register_9_q, register_10_q, register_11_q, register_12_q, register_13_q,
       register_14_q, register_15_q, register_16_q, register_17_q, register_18_q, register_19_q,
       register_20_q, register_21_q, register_22_q, register_23_q, register_24_q, register_25_q,
       register_26_q, register_27_q, register_28_q, register_29_q, register_30_q, register_31_q,
       register_32_q;

  Decoder #(.select(5), .enable("false")) decoder_1 (
    .out0(decoder_1_out0), .out1(decoder_1_out1), .out2(decoder_1_out2), .out3(decoder_1_out3),
    .out4(decoder_1_out4), .out5(decoder_1_out5), .out6(decoder_1_out6), .out7(decoder_1_out7),
    .out8(decoder_1_out8), .out9(decoder_1_out9), .out10(decoder_1_out10), .out11(decoder_1_out11),
    .out12(decoder_1_out12), .out13(decoder_1_out13), .out14(decoder_1_out14), .out15(decoder_1_out15),
    .out16(decoder_1_out16), .out17(decoder_1_out17), .out18(decoder_1_out18), .out19(decoder_1_out19),
    .out20(decoder_1_out20), .out21(decoder_1_out21), .out22(decoder_1_out22), .out23(decoder_1_out23),
    .out24(decoder_1_out24), .out25(decoder_1_out25), .out26(decoder_1_out26), .out27(decoder_1_out27),
    .out28(decoder_1_out28), .out29(decoder_1_out29), .out30(decoder_1_out30), .out31(decoder_1_out31),
    .sel(Write_Address));
  and and_1 (and_1_out, decoder_1_out0, Reg_Write);
  and and_2 (and_2_out, decoder_1_out1, Reg_Write);
  and and_3 (and_3_out, decoder_1_out2, Reg_Write);
  and and_4 (and_4_out, decoder_1_out3, Reg_Write);
  and and_5 (and_5_out, decoder_1_out4, Reg_Write);
  and and_6 (and_6_out, decoder_1_out5, Reg_Write);
  and and_7 (and_7_out, decoder_1_out6, Reg_Write);
  and and_8 (and_8_out, decoder_1_out7, Reg_Write);
  and and_9 (and_9_out, decoder_1_out8, Reg_Write);
  and and_10 (and_10_out, decoder_1_out9, Reg_Write);
  and and_11 (and_11_out, decoder_1_out10, Reg_Write);
  and and_12 (and_12_out, decoder_1_out11, Reg_Write);
  and and_13 (and_13_out, decoder_1_out12, Reg_Write);
  and and_14 (and_14_out, decoder_1_out13, Reg_Write);
  and and_15 (and_15_out, decoder_1_out14, Reg_Write);
  and and_16 (and_16_out, decoder_1_out15, Reg_Write);
  and and_17 (and_17_out, decoder_1_out16, Reg_Write);
  and and_18 (and_18_out, decoder_1_out17, Reg_Write);
  and and_19 (and_19_out, decoder_1_out18, Reg_Write);
  and and_20 (and_20_out, decoder_1_out19, Reg_Write);
  and and_21 (and_21_out, decoder_1_out20, Reg_Write);
  and and_22 (and_22_out, decoder_1_out21, Reg_Write);
  and and_23 (and_23_out, decoder_1_out22, Reg_Write);
  and and_24 (and_24_out, decoder_1_out23, Reg_Write);
  and and_25 (and_25_out, decoder_1_out24, Reg_Write);
  and and_26 (and_26_out, decoder_1_out25, Reg_Write);
  and and_27 (and_27_out, decoder_1_out26, Reg_Write);
  and and_28 (and_28_out, decoder_1_out27, Reg_Write);
  and and_29 (and_29_out, decoder_1_out28, Reg_Write);
  and and_30 (and_30_out, decoder_1_out29, Reg_Write);
  and and_31 (and_31_out, decoder_1_out30, Reg_Write);
  and and_32 (and_32_out, decoder_1_out31, Reg_Write);
  Register #(.width(32)) register_1 (.D(Data_In), .en(and_1_out), .Q(register_1_q), .clk(in_6));  // open: clr
  Register #(.width(32)) register_2 (.D(Data_In), .en(and_2_out), .Q(register_2_q), .clk(in_6));  // open: clr
  Register #(.width(32)) register_3 (.D(Data_In), .en(and_3_out), .Q(register_3_q), .clk(in_6));  // open: clr
  Register #(.width(32)) register_4 (.D(Data_In), .en(and_4_out), .Q(register_4_q), .clk(in_6));  // open: clr
  Register #(.width(32)) register_5 (.D(Data_In), .en(and_5_out), .Q(register_5_q), .clk(in_6));  // open: clr
  Register #(.width(32)) register_6 (.D(Data_In), .en(and_6_out), .Q(register_6_q), .clk(in_6));  // open: clr
  Register #(.width(32)) register_7 (.D(Data_In), .en(and_7_out), .Q(register_7_q), .clk(in_6));  // open: clr
  Register #(.width(32)) register_8 (.D(Data_In), .en(and_8_out), .Q(register_8_q), .clk(in_6));  // open: clr
  Register #(.width(32)) register_9 (.D(Data_In), .en(and_9_out), .Q(register_9_q), .clk(in_6));  // open: clr
  Register #(.width(32)) register_10 (.D(Data_In), .en(and_10_out), .Q(register_10_q), .clk(in_6));  // open: clr
  Register #(.width(32)) register_11 (.D(Data_In), .en(and_11_out), .Q(register_11_q), .clk(in_6));  // open: clr
  Register #(.width(32)) register_12 (.D(Data_In), .en(and_12_out), .Q(register_12_q), .clk(in_6));  // open: clr
  Register #(.width(32)) register_13 (.D(Data_In), .en(and_13_out), .Q(register_13_q), .clk(in_6));  // open: clr
  Register #(.width(32)) register_14 (.D(Data_In), .en(and_14_out), .Q(register_14_q), .clk(in_6));  // open: clr
  Register #(.width(32)) register_15 (.D(Data_In), .en(and_15_out), .Q(register_15_q), .clk(in_6));  // open: clr
  Register #(.width(32)) register_16 (.D(Data_In), .en(and_16_out), .Q(register_16_q), .clk(in_6));  // open: clr
  Register #(.width(32)) register_17 (.D(Data_In), .en(and_17_out), .Q(register_17_q), .clk(in_6));  // open: clr
  Register #(.width(32)) register_18 (.D(Data_In), .en(and_18_out), .Q(register_18_q), .clk(in_6));  // open: clr
  Register #(.width(32)) register_19 (.D(Data_In), .en(and_19_out), .Q(register_19_q), .clk(in_6));  // open: clr
  Register #(.width(32)) register_20 (.D(Data_In), .en(and_20_out), .Q(register_20_q), .clk(in_6));  // open: clr
  Register #(.width(32)) register_21 (.D(Data_In), .en(and_21_out), .Q(register_21_q), .clk(in_6));  // open: clr
  Register #(.width(32)) register_22 (.D(Data_In), .en(and_22_out), .Q(register_22_q), .clk(in_6));  // open: clr
  Register #(.width(32)) register_23 (.D(Data_In), .en(and_23_out), .Q(register_23_q), .clk(in_6));  // open: clr
  Register #(.width(32)) register_24 (.D(Data_In), .en(and_24_out), .Q(register_24_q), .clk(in_6));  // open: clr
  Register #(.width(32)) register_25 (.D(Data_In), .en(and_25_out), .Q(register_25_q), .clk(in_6));  // open: clr
  Register #(.width(32)) register_26 (.D(Data_In), .en(and_26_out), .Q(register_26_q), .clk(in_6));  // open: clr
  Register #(.width(32)) register_27 (.D(Data_In), .en(and_27_out), .Q(register_27_q), .clk(in_6));  // open: clr
  Register #(.width(32)) register_28 (.D(Data_In), .en(and_28_out), .Q(register_28_q), .clk(in_6));  // open: clr
  Register #(.width(32)) register_29 (.D(Data_In), .en(and_29_out), .Q(register_29_q), .clk(in_6));  // open: clr
  Register #(.width(32)) register_30 (.D(Data_In), .en(and_30_out), .Q(register_30_q), .clk(in_6));  // open: clr
  Register #(.width(32)) register_31 (.D(Data_In), .en(and_31_out), .Q(register_31_q), .clk(in_6));  // open: clr
  Register #(.width(32)) register_32 (.D(Data_In), .en(and_32_out), .Q(register_32_q), .clk(in_6));  // open: clr
  Multiplexer #(.select(5), .width(32), .enable("false")) multiplexer_1 (
    .in0(register_1_q), .in1(register_2_q), .in2(register_3_q), .in3(register_4_q), .in4(register_5_q),
    .in5(register_6_q), .in6(register_7_q), .in7(register_8_q), .in8(register_9_q), .in9(register_10_q),
    .in10(register_11_q), .in11(register_12_q), .in12(register_13_q), .in13(register_14_q),
    .in14(register_15_q), .in15(register_16_q), .in16(register_17_q), .in17(register_18_q),
    .in18(register_19_q), .in19(register_20_q), .in20(register_21_q), .in21(register_22_q),
    .in22(register_23_q), .in23(register_24_q), .in24(register_25_q), .in25(register_26_q),
    .in26(register_27_q), .in27(register_28_q), .in28(register_29_q), .in29(register_30_q),
    .in30(register_31_q), .in31(register_32_q), .out(Data_Out_1), .sel(Read_Address_1));
  Multiplexer #(.select(5), .width(32), .enable("false")) multiplexer_2 (
    .in0(register_1_q), .in1(register_2_q), .in2(register_3_q), .in3(register_4_q), .in4(register_5_q),
    .in5(register_6_q), .in6(register_7_q), .in7(register_8_q), .in8(register_9_q), .in9(register_10_q),
    .in10(register_11_q), .in11(register_12_q), .in12(register_13_q), .in13(register_14_q),
    .in14(register_15_q), .in15(register_16_q), .in16(register_17_q), .in17(register_18_q),
    .in18(register_19_q), .in19(register_20_q), .in20(register_21_q), .in21(register_22_q),
    .in22(register_23_q), .in23(register_24_q), .in24(register_25_q), .in25(register_26_q),
    .in26(register_27_q), .in27(register_28_q), .in28(register_29_q), .in29(register_30_q),
    .in30(register_31_q), .in31(register_32_q), .out(Data_Out_2), .sel(Read_Address_2));
endmodule
